// Logisim project TallerLogica_Combinatorios_grupo_5.circ as structural Verilog: 10 circuits, main circuit sumador_simple
module sumador_simple (
  input  A,
  input  B,
  output S,
  output Cout
);

  and and_1 (Cout, A, B);
  xor xor_1 (S, A, B);
endmodule

module sumador_completo (
  input  Cin,
  input  A,
  input  B,
  output S,
  output Cout
);

  wire sumador_simple_1_cout, sumador_simple_1_s, sumador_simple_2_cout;

  sumador_simple sumador_simple_1 (.A(A), .B(B), .Cout(sumador_simple_1_cout), .S(sumador_simple_1_s));
  sumador_simple sumador_simple_2 (.A(Cin), .B(sumador_simple_1_s), .Cout(sumador_simple_2_cout), .S(S));
  or or_1 (Cout, sumador_simple_2_cout, sumador_simple_1_cout);
endmodule

module sumador_4 (
  input  Cin,
  input  [3:0] A,
  input  [3:0] B,
  output [3:0] S,
  output Cout
);

  wire sumador_completo_1_cout, sumador_completo_2_cout, sumador_completo_3_cout;

  sumador_completo sumador_completo_1 (.A(A[0]), .B(B[0]), .Cin(Cin), .S(S[0]), .Cout(sumador_completo_1_cout));
  sumador_completo sumador_completo_2 (
    .A(A[1]), .B(B[1]), .Cin(sumador_completo_1_cout), .S(S[1]), .Cout(sumador_completo_2_cout));
  sumador_completo sumador_completo_3 (
    .A(A[2]), .B(B[2]), .Cin(sumador_completo_2_cout), .S(S[2]), .Cout(sumador_completo_3_cout));
  sumador_completo sumador_completo_4 (.A(A[3]), .B(B[3]), .Cin(sumador_completo_3_cout), .S(S[3]), .Cout(Cout));
  Hex_Digit_Display hex_digit_display_1 (.value(S));  // open: dp
endmodule

module comparador_cero (
  input  [3:0] A,
  output Z
);

  wire nor_1_out, nor_2_out;

  nor nor_1 (nor_1_out, A[0], A[1]);
  nor nor_2 (nor_2_out, A[2], A[3]);
  and and_1 (Z, nor_1_out, nor_2_out);
endmodule

module sumador_flags (
  input  Cin,
  input  [3:0] A,
  input  [3:0] B,
  output [3:0] S,
  output N,
  output Z,
  output V,
  output C
);

  wire and_1_out, nand_1_out, nor_1_out, nor_2_out;

  sumador_4 sumador_4_1 (.A(A), .B(B), .Cin(Cin), .Cout(C), .S({N, S[2:0]}));
  nand nand_1 (nand_1_out, A[3], B[3]);
  nor nor_1 (nor_1_out, A[3], B[3]);
  nor nor_2 (nor_2_out, N, nand_1_out);
  and and_1 (and_1_out, N, nor_1_out);
  Hex_Digit_Display hex_digit_display_1 (.value({N, S[2:0]}));  // open: dp
  comparador_cero comparador_cero_1 (.A({N, S[2:0]}), .Z(Z));
  or or_1 (V, nor_2_out, and_1_out);

  assign S[3] = N;
endmodule

module incrementador_4 (
  input  [3:0] A,
  output [3:0] S
);

  sumador_4 sumador_4_1 (.A(A), .B(4'b0001), .S(S));  // open: Cin, Cout
  Hex_Digit_Display hex_digit_display_1 (.value(S));  // open: dp
endmodule

module inversor_4 (
  input  [3:0] A,
  input  INV,
  output [3:0] S
);

  wire sumador_completo_1_cout, sumador_completo_2_cout, sumador_completo_3_cout;
  wire [3:0] not_1_out, sumador_completo_1_s;

  assign not_1_out = ~A;  // NOT_Gate not_1, 4 bits wide
  sumador_completo sumador_completo_1 (
    .A(not_1_out[0]), .B(INV), .S(sumador_completo_1_s[0]), .Cout(sumador_completo_1_cout));  // open: Cin
  sumador_completo sumador_completo_2 (
    .A(sumador_completo_1_cout), .B(not_1_out[1]), .S(sumador_completo_1_s[1]), .Cout(sumador_completo_2_cout));  // open: Cin
  sumador_completo sumador_completo_3 (
    .A(sumador_completo_2_cout), .B(not_1_out[2]), .S(sumador_completo_1_s[2]), .Cout(sumador_completo_3_cout));  // open: Cin
  Multiplexer #(.width(4)) multiplexer_1 (.in0(A), .in1(sumador_completo_1_s), .out(S), .sel(INV));
  sumador_completo sumador_completo_4 (
    .A(sumador_completo_3_cout), .B(not_1_out[3]), .S(sumador_completo_1_s[3]));  // open: Cin, Cout
  Hex_Digit_Display hex_digit_display_1 (.value(S));  // open: dp
endmodule

module ALU (
  input  [3:0] A,
  input  [3:0] B,
  input  [1:0] OP,
  output N,
  output Z,
  output V,
  output C,
  output [3:0] S
);

  Multiplexer #(.select(2), .width(4)) multiplexer_1 (.out(S), .sel(OP));  // open: in0, in1, in2, in3
  Hex_Digit_Display hex_digit_display_1 (.value(S));  // open: dp
endmodule

module verificador (
  output [3:0] out_1,
  output [3:0] out_2,
  output [1:0] out_3,
  output halt,
  output N,
  output Z,
  output V,
  output C,
  output [3:0] res
);

  wire clock_1_out;

  Clock clock_1 (.out(clock_1_out));
  Counter #(.max('h3ff), .width(10)) counter_1 (
    .clk(clock_1_out), .carry(halt), .Q({out_3, out_2, out_1}));  // open: clr, load, up, count, D
  ALU alu_1 (.A(out_1), .B(out_2), .OP(out_3), .N(N), .Z(Z), .V(V), .C(C), .S(res));
endmodule

module and_aux (
  input  [3:0] A,
  input  [3:0] B
);

  wire and_1_out, and_2_out, and_3_out, and_4_out;

  and and_1 (and_1_out, A[0], B[0]);
  and and_2 (and_2_out, A[1], B[1]);
  and and_3 (and_3_out, A[2], B[2]);
  and and_4 (and_4_out, A[3], B[3]);
endmodule
