// Logisim project resuelto.circ as structural Verilog: 13 circuits, main circuit verificador
module sumador_simple (
  input  A,
  input  B,
  output S,
  output Cout
);

  xor xor_1 (S, A, B);
  and and_1 (Cout, A, B);
endmodule

module sumador_completo (
  input  Cin,
  input  A,
  input  B,
  output S,
  output Cout
);

  wire sumador_simple_1_cout, sumador_simple_1_s, sumador_simple_2_cout;

  sumador_simple sumador_simple_1 (.A(A), .B(B), .S(sumador_simple_1_s), .Cout(sumador_simple_1_cout));
  sumador_simple sumador_simple_2 (.A(Cin), .B(sumador_simple_1_s), .S(S), .Cout(sumador_simple_2_cout));
  or or_1 (Cout, sumador_simple_2_cout, sumador_simple_1_cout);
endmodule

module sumador_4 (
  input  Cin,
  input  [3:0] A,
  input  [3:0] B,
  output [3:0] S,
  output Cout
);

  wire sumador_completo_1_cout, sumador_completo_2_cout, sumador_completo_3_cout;

  sumador_completo sumador_completo_1 (.Cin(Cin), .A(A[0]), .B(B[0]), .S(S[0]), .Cout(sumador_completo_1_cout));
  sumador_completo sumador_completo_2 (
    .Cin(sumador_completo_1_cout), .A(A[1]), .B(B[1]), .S(S[1]), .Cout(sumador_completo_2_cout));
  sumador_completo sumador_completo_3 (
    .Cin(sumador_completo_2_cout), .A(A[2]), .B(B[2]), .S(S[2]), .Cout(sumador_completo_3_cout));
  sumador_completo sumador_completo_4 (.Cin(sumador_completo_3_cout), .A(A[3]), .B(B[3]), .S(S[3]), .Cout(Cout));
  Hex_Digit_Display hex_digit_display_1 (.value(S));  // open: dp
endmodule

module comparador_cero (
  input  [3:0] A,
  output Z
);

  wire and_1_out, and_2_out, not_1_out, not_2_out, not_3_out, not_4_out;

  not not_1 (not_1_out, A[0]);
  not not_2 (not_2_out, A[1]);
  and and_1 (and_1_out, not_1_out, not_2_out);
  and and_2 (and_2_out, and_1_out, not_3_out);
  not not_3 (not_3_out, A[2]);
  not not_4 (not_4_out, A[3]);
  and and_3 (Z, and_2_out, not_4_out);
endmodule

module sumador_flags (
  input  Cin,
  input  [3:0] A,
  input  [3:0] B,
  output [3:0] S,
  output N,
  output Z,
  output V,
  output C
);

  wire and_1_out, and_2_out, and_3_out, and_4_out, not_1_out, not_2_out, not_3_out;

  sumador_4 sumador_4_1 (.Cin(Cin), .A(A), .B(B), .S({N, S[2:0]}), .Cout(C));
  not not_1 (not_1_out, A[3]);
  not not_2 (not_2_out, B[3]);
  and and_1 (and_1_out, A[3], B[3]);
  and and_2 (and_2_out, not_1_out, not_2_out);
  Hex_Digit_Display hex_digit_display_1 (.value({N, S[2:0]}));  // open: dp
  not not_3 (not_3_out, N);
  comparador_cero comparador_cero_1 (.A({N, S[2:0]}), .Z(Z));
  and and_3 (and_3_out, not_3_out, and_1_out);
  and and_4 (and_4_out, N, and_2_out);
  or or_1 (V, and_3_out, and_4_out);

  assign S[3] = N;
endmodule

module incrementador_4 (
  input  [3:0] A,
  output [3:0] S
);

  wire sumador_4_1_cout;

  sumador_4 sumador_4_1 (.Cin(1'b0), .A(4'b0001), .B(A), .S(S), .Cout(sumador_4_1_cout));
  LED led_1 (.in(sumador_4_1_cout));
  Hex_Digit_Display hex_digit_display_1 (.value(S));  // open: dp
endmodule

module inversor_4 (
  input  [3:0] A,
  input  INV,
  output [3:0] S
);

  wire not_1_out, not_2_out, not_3_out, not_4_out, sumador_simple_1_cout, sumador_simple_2_cout,
       sumador_simple_3_cout;
  wire [3:0] sumador_simple_1_s;

  not not_1 (not_1_out, A[0]);
  not not_2 (not_2_out, A[1]);
  not not_3 (not_3_out, A[2]);
  not not_4 (not_4_out, A[3]);
  sumador_simple sumador_simple_1 (.A(not_1_out), .B(INV), .S(sumador_simple_1_s[0]), .Cout(sumador_simple_1_cout));
  sumador_simple sumador_simple_2 (
    .A(sumador_simple_1_cout), .B(not_2_out), .S(sumador_simple_1_s[1]), .Cout(sumador_simple_2_cout));
  sumador_simple sumador_simple_3 (
    .A(sumador_simple_2_cout), .B(not_3_out), .S(sumador_simple_1_s[2]), .Cout(sumador_simple_3_cout));
  sumador_simple sumador_simple_4 (.A(sumador_simple_3_cout), .B(not_4_out), .S(sumador_simple_1_s[3]));  // open: Cout
  Multiplexer #(.width(4)) multiplexer_1 (.in0(A), .in1(sumador_simple_1_s), .out(S), .sel(INV));
  Hex_Digit_Display hex_digit_display_1 (.value(S));  // open: dp
endmodule

module ALU (
  input  [3:0] A,
  input  [3:0] B,
  input  [1:0] OP,
  output [3:0] S,
  output N,
  output Z,
  output V,
  output C
);

  wire operacion_and_1_c, operacion_and_1_n, operacion_and_1_v, operacion_and_1_z, operacion_or_1_c,
       operacion_or_1_n, operacion_or_1_v, operacion_or_1_z, operacion_resta_1_c, operacion_resta_1_n,
       operacion_resta_1_v, operacion_resta_1_z, sumador_flags_1_c, sumador_flags_1_n, sumador_flags_1_v,
       sumador_flags_1_z;
  wire [3:0] operacion_and_1_s, operacion_or_1_s, operacion_resta_1_s, sumador_flags_1_s;

  sumador_flags sumador_flags_1 (
    .A(A), .B(B), .S(sumador_flags_1_s), .N(sumador_flags_1_n), .Z(sumador_flags_1_z), .V(sumador_flags_1_v),
    .C(sumador_flags_1_c));  // open: Cin
  operacion_OR operacion_or_1 (
    .A(A), .B(B), .S(operacion_or_1_s), .N(operacion_or_1_n), .Z(operacion_or_1_z), .V(operacion_or_1_v),
    .C(operacion_or_1_c));
  operacion_RESTA operacion_resta_1 (
    .A(A), .B(B), .S(operacion_resta_1_s), .N(operacion_resta_1_n), .Z(operacion_resta_1_z),
    .V(operacion_resta_1_v), .C(operacion_resta_1_c));
  operacion_AND operacion_and_1 (
    .A(A), .B(B), .S(operacion_and_1_s), .N(operacion_and_1_n), .Z(operacion_and_1_z), .V(operacion_and_1_v),
    .C(operacion_and_1_c));
  Multiplexer #(.select(2), .width(4)) multiplexer_1 (
    .in0(sumador_flags_1_s), .in1(operacion_resta_1_s), .in2(operacion_and_1_s), .in3(operacion_or_1_s),
    .out(S), .sel(OP));
  Multiplexer #(.select(2)) multiplexer_2 (
    .in0(sumador_flags_1_n), .in1(operacion_resta_1_n), .in2(operacion_and_1_n), .in3(operacion_or_1_n),
    .out(N), .sel(OP));
  Multiplexer #(.select(2)) multiplexer_3 (
    .in0(sumador_flags_1_z), .in1(operacion_resta_1_z), .in2(operacion_and_1_z), .in3(operacion_or_1_z),
    .out(Z), .sel(OP));
  Multiplexer #(.select(2)) multiplexer_4 (
    .in0(sumador_flags_1_v), .in1(operacion_resta_1_v), .in2(operacion_and_1_v), .in3(operacion_or_1_v),
    .out(V), .sel(OP));
  Multiplexer #(.select(2)) multiplexer_5 (
    .in0(sumador_flags_1_c), .in1(operacion_resta_1_c), .in2(operacion_and_1_c), .in3(operacion_or_1_c),
    .out(C), .sel(OP));
  Hex_Digit_Display hex_digit_display_1 (.value(S));  // open: dp
endmodule

module verificador (
  output [3:0] out_1,
  output [3:0] out_2,
  output [1:0] out_3,
  output halt,
  output N,
  output Z,
  output V,
  output C,
  output [3:0] res
);

  wire clock_1_out;

  Clock clock_1 (.out(clock_1_out));
  Counter #(.max('h3ff), .width(10)) counter_1 (
    .clk(clock_1_out), .carry(halt), .Q({out_3, out_2, out_1}));  // open: clr, load, up, count, D
  ALU alu_1 (.A(out_1), .B(out_2), .OP(out_3), .S(res), .N(N), .Z(Z), .V(V), .C(C));
endmodule

module operacion_AND (
  input  [3:0] A,
  input  [3:0] B,
  output [3:0] S,
  output N,
  output Z,
  output V,
  output C
);

  and and_1 (S[0], A[0], B[0]);
  and and_2 (S[1], A[1], B[1]);
  and and_3 (S[2], A[2], B[2]);
  and and_4 (N, A[3], B[3]);
  comparador_cero comparador_cero_1 (.A({N, S[2:0]}), .Z(Z));

  assign C = 1'b0;
  assign S[3] = N;
  assign V = 1'b0;
endmodule

module operacion_OR (
  input  [3:0] A,
  input  [3:0] B,
  output [3:0] S,
  output N,
  output Z,
  output V,
  output C
);

  or or_1 (S[0], A[0], B[0]);
  or or_2 (S[1], A[1], B[1]);
  or or_3 (S[2], A[2], B[2]);
  or or_4 (N, A[3], B[3]);
  comparador_cero comparador_cero_1 (.A({N, S[2:0]}), .Z(Z));

  assign C = 1'b0;
  assign S[3] = N;
  assign V = 1'b0;
endmodule

module operacion_RESTA (
  input  [3:0] A,
  input  [3:0] B,
  output [3:0] S,
  output N,
  output Z,
  output V,
  output C
);

  wire and_1_out, and_2_out, and_3_out, and_4_out, comparador_cero_2_z, comparador_menos_ocho_1_z, not_2_out,
       not_3_out, not_4_out, not_5_out, not_6_out, not_7_out, or_1_out, sumador_4_1_cout;
  wire [3:0] incrementador_4_1_s, not_1_out;

  assign not_1_out = ~B;  // NOT_Gate not_1, 4 bits wide
  incrementador_4 incrementador_4_1 (.A(not_1_out), .S(incrementador_4_1_s));
  sumador_4 sumador_4_1 (.Cin(1'b0), .A(A), .B(incrementador_4_1_s), .S({N, S[2:0]}), .Cout(sumador_4_1_cout));
  not not_2 (not_2_out, sumador_4_1_cout);
  not not_3 (not_3_out, A[3]);
  not not_4 (not_4_out, incrementador_4_1_s[3]);
  and and_1 (and_1_out, A[3], incrementador_4_1_s[3]);
  and and_2 (and_2_out, not_3_out, not_4_out);
  Hex_Digit_Display hex_digit_display_1 (.value({N, S[2:0]}));  // open: dp
  not not_5 (not_5_out, N);
  comparador_menos_ocho comparador_menos_ocho_1 (.A(B), .Z(comparador_menos_ocho_1_z));
  comparador_cero comparador_cero_1 (.A({N, S[2:0]}), .Z(Z));
  and and_3 (and_3_out, not_5_out, and_1_out);
  and and_4 (and_4_out, N, and_2_out);
  or or_1 (or_1_out, and_3_out, and_4_out);
  comparador_cero comparador_cero_2 (.A(B), .Z(comparador_cero_2_z));
  not not_6 (not_6_out, or_1_out);
  not not_7 (not_7_out, not_2_out);
  Multiplexer multiplexer_1 (.in0(or_1_out), .in1(not_6_out), .out(V), .sel(comparador_menos_ocho_1_z));
  Multiplexer multiplexer_2 (.in0(not_2_out), .in1(not_7_out), .out(C), .sel(comparador_cero_2_z));

  assign S[3] = N;
endmodule

module comparador_menos_ocho (
  input  [3:0] A,
  output Z
);

  wire and_1_out, and_2_out, not_1_out, not_2_out, not_3_out;

  not not_1 (not_1_out, A[0]);
  not not_2 (not_2_out, A[1]);
  and and_1 (and_1_out, not_1_out, not_2_out);
  and and_2 (and_2_out, and_1_out, not_3_out);
  not not_3 (not_3_out, A[2]);
  and and_3 (Z, and_2_out, A[3]);
endmodule
